# Fritzing sketch temp_logger (saved by Fritzing 0.9.1b)
circuit board: 8.46667cm x 5.64444cm
breadboards: 1

parts:
  IC1 = MICROCONTROLLER [package=dil28-3-simon]
  IC2 = 25LC1024 [package=THT]
  R1 = Temperature Sensor (Thermistor) [thermistor_type=NTC package=THT]
  R2 = Resistor [tolerance=±5% resistance=47k package=THT]
  Y1 = CRYSTAL [package=tc26h]
  R3 = Resistor [tolerance=±1% resistance=10k package=THT]
  C4 = Ceramic Capacitor [capacitance="100 nF" package="200 mil [THT, multilayer]"]
  C3 = Ceramic Capacitor [capacitance=10pF package="200 mil [THT, multilayer]"]
  C2 = Ceramic Capacitor [capacitance=8pF package="200 mil [THT, multilayer]"]
  R4 = Resistor [tolerance=±5% resistance=2.2k package=THT]
  R5 = Resistor [tolerance=±5% resistance=2.2k package=THT]
  R6 = Resistor [tolerance=±5% resistance=10k package=THT]
  part = DC Power [voltage=5V]
  IC3 = MCP7940M [chip_label=MCP7940 package="DIP (Dual Inline) [THT]"]

nets:
  N1: IC1.PD2(INT0), R6.Pin_0, IC3.MFP
  5V: IC1.VCC, IC2.+V, R1.pin_0, R2.Pin_0, C4.0, R4.Pin_1, R5.Pin_1, R6.Pin_1, part.V+, IC3.VCC
  GND: IC1.GND, IC1.AGND, IC2.WP_-_Write_Protect, IC2.0V, R3.Pin_1, C4.1, C3.0, C2.1, part.V-, IC3.VSS
  N2: IC1.PD6(AIN0), R1.pin_1, R3.Pin_0
  N3: IC1.PB2(SS_OC1B), IC2.CS_-_Chip_Select, R2.Pin_1
  N4: IC1.PB3(MOSI_OC2), IC2.SI_-_Data_In
  N5: IC1.PB4(MISO), IC2.SO_-_Data_Out
  N6: IC1.PB5(SCK), IC2.SCK_-_SPI_Clock
  N7: IC1.PC4(ADC4_SDA), R4.Pin_0, IC3.SDA
  N8: IC1.PC5(ADC5_SCL), R5.Pin_0, IC3.SCL
  N9: Y1.1, C3.1, IC3.X1
  N10: Y1.2, C2.0, IC3.X2

custom parts:
  MCP7940M: MCP7940M I2C RTC
